# Fritzing sketch Smartlock_UNO (saved by Fritzing 0.9.3b)
breadboards: 1

parts:
  Part1 = Arduino Uno (Rev3)
  KEYPAD2 = Membrane Matrix Keypad
  SW1 = DIP SWITCH [package=dipswitch-02]
  LED1 = LEDs [package=led10mm]
  LED2 = LEDs [package=led10mm]
  BAT1 = BC9VPC [package=bc9vpc]
  R1 = Resistor [tolerance=±5% resistance=220 package=THT]
  R2 = Resistor [tolerance=±5% resistance=220 package="1206 [SMD]"]

nets:
  N1: Part1.D8, KEYPAD2.2
  N2: Part1.D9_PWM, KEYPAD2.1
  N3: Part1.D11_PWM/MOSI, R2.Pin_1
  N4: Part1.GND, LED1.C, LED2.C, BAT1.V-
  N5: Part1.D2, R1.Pin_1
  N6: Part1.D3_PWM, KEYPAD2.7
  N7: Part1.D4, KEYPAD2.6
  N8: Part1.D5_PWM, KEYPAD2.5
  N9: Part1.D6_PWM, KEYPAD2.4
  N10: Part1.D7, KEYPAD2.3
  N11: Part1.5V, SW1.1
  N12: SW1.4, BAT1.V+
  N13: LED1.A, R2.Pin_0
  N14: LED2.A, R1.Pin_0

custom parts:
  Membrane Matrix Keypad: Membrane Matrix 3x4 Keypad
